# Fritzing sketch DemoControlPanel (saved by Fritzing 0.9.5d)
breadboards: 1

parts:
  J1 = Generic shrouded header - 64 pins [form="♂ (shrouded male)" package=THT]
  LED1 = Red LED - 5mm [package="5 mm [THT]"]
  R1 = 220 Ω Resistor [package="0603 [SMD]"]
  S1 = Pushbutton [package="[THT]"]
  S2 = Pushbutton [package="[THT]"]
  S3 = Pushbutton [package="[THT]"]
  S4 = Pushbutton [package="[THT]"]
  S5 = Pushbutton [package="[THT]"]
  S6 = Pushbutton [package="[THT]"]
  S7 = Pushbutton [package="[THT]"]
  LED2 = Red LED - 5mm [package="5 mm [THT]"]
  LED3 = Red LED - 5mm [package="5 mm [THT]"]
  LED4 = Red LED - 5mm [package="5 mm [THT]"]
  R2 = 220 Ω Resistor [package="0603 [SMD]"]
  LED5 = Red LED - 5mm [package="5 mm [THT]"]
  LED6 = Red LED - 5mm [package="5 mm [THT]"]
  LED7 = Red LED - 5mm [package="5 mm [THT]"]
  R3 = 220 Ω Resistor [package="0603 [SMD]"]
  R4 = 220 Ω Resistor [package="0603 [SMD]"]
  R5 = 220 Ω Resistor [package="0603 [SMD]"]
  R6 = 220 Ω Resistor [package="0603 [SMD]"]
  R7 = 220 Ω Resistor [package="0603 [SMD]"]

nets:
  3.3V: J1.pin1, J1.pin2
  N1: J1.pin3, R1.Pin_0
  N2: J1.pin4, R2.Pin_0
  N3: J1.pin5, R3.Pin_0
  N4: J1.pin6, R4.Pin_0
  N5: J1.pin7, R5.Pin_0
  N6: J1.pin8, R6.Pin_0
  N7: J1.pin9, R7.Pin_0
  N8: J1.pin56, S1.Pin_3, S1.Pin_4
  N9: J1.pin57, S2.Pin_3, S2.Pin_4
  N10: J1.pin58, S3.Pin_3, S3.Pin_4
  N11: J1.pin59, S4.Pin_3, S4.Pin_4
  N12: J1.pin60, S5.Pin_3, S5.Pin_4
  N13: J1.pin61, S6.Pin_3, S6.Pin_4
  N14: J1.pin62, S7.Pin_3, S7.Pin_4
  GND: J1.pin63, J1.pin64, LED1.cathode, S1.Pin_1, S1.Pin_2, S2.Pin_1, S2.Pin_2, S3.Pin_1, S3.Pin_2, S4.Pin_1, S4.Pin_2, S5.Pin_1, S5.Pin_2, S6.Pin_1, S6.Pin_2, S7.Pin_1, S7.Pin_2, LED2.cathode, LED3.cathode, LED4.cathode, LED5.cathode, LED6.cathode, LED7.cathode
  N15: LED1.anode, R1.Pin_1
  N16: LED2.anode, R2.Pin_1
  N17: LED3.anode, R3.Pin_1
  N18: LED4.anode, R4.Pin_1
  N19: LED5.anode, R5.Pin_1
  N20: LED6.anode, R6.Pin_1
  N21: LED7.anode, R7.Pin_1

notes:
  All wires and resistors
  are on the under (foil)
  side. Only the connector, LEDs and
  switches are on the top (component) side.

custom parts:
  Generic shrouded header - 64 pins: Generic shrouded header
  Red LED - 5mm: A generic red LED (~1.8V)
  220 Ω Resistor: A generic resistor (0.25W)
